// Digital circuit meio_somador_1bit.dig as structural Verilog
module meio_somador_1bit (
  input  A,
  input  B,
  output S,
  output C_out
);

  xor xor_1 (S, A, B);
  and and_1 (C_out, A, B);
endmodule
