// Digital circuit somador_completo_1bit_usando_meio_somador.dig as structural Verilog
module somador_completo_1bit_usando_meio_somador (
  input  A,
  input  B,
  input  C_in,
  output S,
  output C_out
);

  wire meio_somador_1bit_1_c_out, meio_somador_1bit_1_s, meio_somador_1bit_2_c_out;

  meio_somador_1bit meio_somador_1bit_1 (.A(A), .B(B), .S(meio_somador_1bit_1_s), .C_out(meio_somador_1bit_1_c_out));
  meio_somador_1bit meio_somador_1bit_2 (.A(C_in), .B(meio_somador_1bit_1_s), .S(S), .C_out(meio_somador_1bit_2_c_out));
  or or_1 (C_out, meio_somador_1bit_2_c_out, meio_somador_1bit_1_c_out);
endmodule
