// Digital circuit somador_completo_4bits.dig as structural Verilog
module somador_completo_4bits (
  input  C_in,
  input  A_0,
  input  A_1,
  input  A_2,
  input  A_3,
  input  B_0,
  input  B_1,
  input  B_2,
  input  B_3,
  output S_0,
  output S_1,
  output S_2,
  output S_3,
  output C_out
);

  wire somador_completo_1bit_1_c_out, somador_completo_1bit_2_c_out, somador_completo_1bit_3_c_out;

  somador_completo_1bit somador_completo_1bit_1 (
    .C_in(C_in), .A(A_0), .B(B_0), .S(S_0), .C_out(somador_completo_1bit_1_c_out));
  somador_completo_1bit somador_completo_1bit_2 (
    .C_in(somador_completo_1bit_1_c_out), .A(A_1), .B(B_1), .S(S_1), .C_out(somador_completo_1bit_2_c_out));
  Seven_Seg_Hex seven_seg_hex_1 (.d({S_3, S_2, S_1, S_0}), .dp(1'b0));
  somador_completo_1bit somador_completo_1bit_3 (
    .C_in(somador_completo_1bit_2_c_out), .A(A_2), .B(B_2), .S(S_2), .C_out(somador_completo_1bit_3_c_out));
  somador_completo_1bit somador_completo_1bit_4 (
    .C_in(somador_completo_1bit_3_c_out), .A(A_3), .B(B_3), .S(S_3), .C_out(C_out));
  LED led_1 (.in(C_out));
endmodule

/* Test case Teste:
            C_in  A_3 A_2 A_1 A_0  B_3 B_2 B_1 B_0  C_out S_3 S_2 S_1 S_0
        repeat(256)  0    bits(4,n>>4)     bits(4,n)        bits(5,(n>>4)+(n&15))
        repeat(256)  1    bits(4,n>>4)     bits(4,n)        bits(5,(n>>4)+(n&15)+1)
*/
